# Fritzing sketch TEJAS 2_PCB (saved by Fritzing 0.9.3b)
perfboards: 1

parts:
  U1 = NodeMCU V1.0  # not connected
  Part1 = InvenSense MPU6050
  Q1 = MOSFET-NCHANNEL [package=to-92]  # not connected
  BAT1 = Battery Holders [package=battery-aa]  # not connected
  LED1 = RGB LED (com. anode, rbg) [package="5 mm [THT]"]  # not connected
  SG1 = Buzzer 12mm [package=buzzer-12mm-ns-kit]  # not connected
  microSD1 = MicroSD Card Module  # not connected
  Part3 = GY-BMEP280 Barometric Pressure Sensor - Breakout
  J2 = Camdenboss CTB0158-2 [part_number=CTB0158-2 package=THT]  # not connected
  J1 = Camdenboss CTB0158-2 [part_number=CTB0158-2 package=THT]  # not connected
  R1 = Resistor [tolerance=±5% resistance=220 package=THT]  # not connected
  R2 = Resistor [tolerance=±5% resistance=220 package=THT]  # not connected

nets:
  N1: Part1.VCC, Part3.SDO
  N2: Part1.GND, Part3.CSB

custom parts:
  NodeMCU V1.0: ESP8266 based NodeMCU
  GY-BMEP280 Barometric Pressure Sensor - Breakout: The BME280 is a chip which was originally designed for the next generation of smartphones. It is made up of a very accurate pressure sensor and an associated temperature sensor which helps calibrate the pressure readings. And just for fun they threw in a pretty solid humidity sensor in there as well! So with an I2C connection you have access to enough weather data to make some pretty good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
