# Fritzing sketch Tejas - Rocket Motor Test Bench (saved by Fritzing 0.9.3b)
perfboards: 1

parts:
  Q1 = MOSFET-NCHANNEL [package=to-92]  # not connected
  Part2 = HX711 Weighing Sensor Module
  LED1 = smd LED [color="Red (633nm)" package="0805 [SMD]"]  # not connected
  J1 = Piezo Speaker  # not connected
  SG1 = Buzzer 12mm [package=buzzer-ccv]  # not connected
  SD_card_module1 = SD Card Module  # not connected
  Part3 = Bluetooth HC-05 Macho
  Part4 = Arduino Uno (Rev3)

nets:
  VCC: Part2.VCC, Part3.VCC, Part4.5V
  GND: Part2.GND, Part3.GND, Part4.GND
  N1: Part3.TXD, Part4.D1/TX
  N2: Part3.RXD, Part4.D0/RX
  N3: Part3.Key, Part4.D4

custom parts:
  SD Card Module: SD Card Module Slot Socket Reader For Arduino ARM MCU
