# Fritzing sketch Tejas-Avionics-PCB (saved by Fritzing 0.9.3b)
circuit board: 10cm x 6cm
perfboards: 1

parts:
  Part1 = Arduino Nano (Rev3.0)
  Part2 = InvenSense MPU6050
  Part3 = GY-BMEP280 Barometric Pressure Sensor - Breakout
  microSD1 = MicroSD Card Module
  Q1 = MOSFET-NCHANNEL [package=to220v]
  Part4 = LilyPad Slide Switch
  BUZZER = Buzzer 12mm [package=buzzer-12mm]
  LED1 = RGB LED (com. anode, rbg) [package="5 mm [THT]"]  # not connected
  FUSE = FUSE [package=fuse_5mm]
  VCC1 = Battery block 9V
  BAT = BATTERY-2 [package=battery-aa]
  R1 = Resistor [tolerance=±5% resistance=1k package="2512 [SMD]"]

nets:
  GND: Part1.GND, Part2.GND, microSD1.GND, Q1.S, Part4.OFF, BUZZER.1, BAT.-2
  N1: Part1.D4, microSD1.CS
  N2: Part1.D5, BUZZER.2
  N3: Part1.D10, R1.Pin_0
  N4: Part1.D11/MOSI, microSD1.MOSI
  N5: Part1.D12/MISO, microSD1.MISO
  N6: Part1.VIN, VCC1.+
  VCC: Part1.5V, Part2.VCC, microSD1.VCC
  N7: Part1.A5, Part2.SCL, Part3.SCL
  N8: Part1.A4, Part2.SDA, Part3.SDA
  3V3: Part1.3V3, Part3.VCC
  N9: Part1.D13/SCK, microSD1.SCK
  N10: Q1.G, R1.Pin_1
  N11: Q1.D, FUSE.2
  N12: Part4.ON, VCC1.-
  N13: FUSE.1, BAT.+2

custom parts:
  GY-BMEP280 Barometric Pressure Sensor - Breakout: The BME280 is a chip which was originally designed for the next generation of smartphones. It is made up of a very accurate pressure sensor and an associated temperature sensor which helps calibrate the pressure readings. And just for fun they threw in a pretty solid humidity sensor in there as well! So with an I2C connection you have access to enough weather data to make some pretty good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
